# Fritzing sketch lcd (saved by Fritzing 0.9.2b)
circuit board: 8.46667cm x 5.64444cm
breadboards: 1

parts:
  U1 = LCD-16X2 [package=lcd-16x2_noholes]
  Raspberry_Pi2 = Raspberry Pi B rev2
  R1 = Resistor [tolerance=±5% resistance=470 package=THT]

nets:
  VSS: U1.VSS, U1.VDD, Raspberry_Pi2.3V3, R1.Pin_1
  N1: U1.VO, U1.R_W, U1.K, Raspberry_Pi2.GND
  N2: U1.RS, Raspberry_Pi2.GPIO_17
  N3: U1.E, Raspberry_Pi2.GPIO_18
  N4: U1.DB4, Raspberry_Pi2.GPIO_27
  N5: U1.DB5, Raspberry_Pi2.GPIO_22
  N6: U1.DB6, Raspberry_Pi2.GPIO_23
  N7: U1.DB7, Raspberry_Pi2.GPIO_24
  N8: U1.A, R1.Pin_0
